# Fritzing sketch Fermentor (saved by Fritzing 1.0.3b)

parts:
  Part1 = Arduino Uno (Rev3) - ICSP
  Part2 = OLED Monochrome 128x32 I2C [part_number=931]

nets:
  N1: Part1.A4/SDA, Part2.SDA
  N2: Part1.A5/SCL, Part2.SCL
  N3: Part1.D2, Part2.RESET
  5V: Part1.5V, Part2.VIN
  GND: Part1.GND, Part2.GND

custom parts:
  OLED Monochrome 128x32 I2C: These displays are small, only about 1" diagonal, but very readable due to the high contrast of an OLED display. This display is made of 128x32 individual white OLED pixels, each one is turned on or off by the controller chip. Because the display makes its own light, no backlight is required. This reduces the power required to run the OLED and is why the display has such high contrast; we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
